# Fritzing sketch keypad (saved by Fritzing 0.9.3b)

parts:
  Part1 = Arduino Uno (Rev3)
  S20 = Pushbutton [package="[THT]"]
  S23 = Pushbutton [package="[THT]"]
  S24 = Pushbutton [package="[THT]"]
  S26 = Pushbutton [package="[THT]"]
  S27 = Pushbutton [package="[THT]"]
  J1 = Piezo Speaker
  LED1 = LED - 5mm [color="Red (633nm)" package="5 mm [THT]"]
  LED2 = LED - 5mm [color="Blue (430nm)" package="5 mm [THT]"]

nets:
  N1: Part1.D8, S24.Pin_1, S24.Pin_2, LED1.cathode, LED2.cathode
  N2: Part1.D9_PWM, S27.Pin_2
  N3: Part1.D10_PWM/SS, S20.Pin_2
  N4: Part1.D11_PWM/MOSI, S23.Pin_2
  N5: Part1.D12/MISO, S26.Pin_2
  N6: Part1.GND, S20.Pin_3, S23.Pin_3, S23.Pin_4, S24.Pin_3, S24.Pin_4, S26.Pin_3, S26.Pin_4, S27.Pin_3, S27.Pin_4, J1.pin1
  N7: Part1.D5_PWM, J1.pin2
  N8: Part1.D6_PWM, LED1.anode
  N9: Part1.D7, LED2.anode
