# Fritzing sketch lcd (saved by Fritzing 0.9.3b)

parts:
  Part1 = Arduino Uno (Rev3)
  LCD1 = LCD screen
  R2 = Rotary Potentiometer (Small) [maximum_resistance=100kΩ package=THT]

nets:
  N1: Part1.A0, LCD1.DB0, LCD1.DB4
  N2: Part1.A1, LCD1.DB1, LCD1.DB5
  N3: Part1.A2, LCD1.DB2, LCD1.DB6
  5V: Part1.A3, Part1.5V, LCD1.VDD, LCD1.DB3, LCD1.DB7, LCD1.LED+, R2.leg2
  N4: Part1.D2, LCD1.E
  N5: Part1.D3_PWM, LCD1.RS
  GND: Part1.GND, LCD1.VSS, LCD1.R/W, LCD1.LED-, R2.leg1
  N6: LCD1.V0, R2.wiper
