# Fritzing sketch rj45 (saved by Fritzing 0.9.3b)

parts:
  Part1 = Arduino Uno (Rev3)
  U2 = RJ45 Jack [package=rj45-8]
  Part2 = Arduino Uno (Rev3)
  U3 = RJ45 Jack [package=rj45-8]

nets:
  N1: Part1.D0/RX, U2.6
  N2: Part1.D1/TX, U2.5
  N3: Part1.GND, U2.7
  N4: U2.2, U3.3
  N5: U2.3, U3.2
  N6: U2.4, U3.1
  N7: Part2.D0/RX, U3.8
  N8: Part2.D1/TX, U3.7
  N9: Part2.GND, U3.6
